# Fritzing sketch final (saved by Fritzing 0.9.3b)
stripboards: 4

parts:
  J404 = male pin header, 39 pins [form="♂ (male)"]
  J405 = male pin header, 39 pins [form="♂ (male)"]
  R336 = Resistor [tolerance=±5% resistance=220 package=THT]
  R337 = Resistor [tolerance=±5% resistance=220 package=THT]
  R338 = Resistor [tolerance=±5% resistance=220 package=THT]
  R339 = Resistor [tolerance=±5% resistance=220 package=THT]
  R340 = Resistor [tolerance=±5% resistance=220 package=THT]
  R341 = Resistor [tolerance=±5% resistance=220 package=THT]
  R342 = Resistor [tolerance=±5% resistance=220 package=THT]
  R343 = Resistor [tolerance=±5% resistance=220 package=THT]
  R344 = Resistor [tolerance=±5% resistance=220 package=THT]
  R345 = Resistor [tolerance=±5% resistance=220 package=THT]
  R346 = Resistor [tolerance=±5% resistance=220 package=THT]
  R347 = Resistor [tolerance=±5% resistance=220 package=THT]
  R348 = Resistor [tolerance=±5% resistance=220 package=THT]
  R349 = Resistor [tolerance=±5% resistance=220 package=THT]
  R350 = Resistor [tolerance=±5% resistance=220 package=THT]
  R351 = Resistor [tolerance=±5% resistance=220 package=THT]
  R352 = Resistor [tolerance=±5% resistance=220 package=THT]
  R353 = Resistor [tolerance=±5% resistance=220 package=THT]
  R354 = Resistor [tolerance=±5% resistance=220 package=THT]
  R355 = Resistor [tolerance=±5% resistance=220 package=THT]
  R356 = Resistor [tolerance=±5% resistance=220 package=THT]
  R357 = Resistor [tolerance=±5% resistance=220 package=THT]
  R358 = Resistor [tolerance=±5% resistance=220 package=THT]
  R359 = Resistor [tolerance=±5% resistance=220 package=THT]
  R360 = Resistor [tolerance=±5% resistance=220 package=THT]
  R361 = Resistor [tolerance=±5% resistance=220 package=THT]
  R362 = Resistor [tolerance=±5% resistance=220 package=THT]
  R363 = Resistor [tolerance=±5% resistance=220 package=THT]
  R364 = Resistor [tolerance=±5% resistance=220 package=THT]
  R365 = Resistor [tolerance=±5% resistance=220 package=THT]
  R366 = Resistor [tolerance=±5% resistance=220 package=THT]
  R367 = Resistor [tolerance=±5% resistance=220 package=THT]
  R368 = Resistor [tolerance=±5% resistance=220 package=THT]
  R369 = Resistor [tolerance=±5% resistance=220 package=THT]
  R370 = Resistor [tolerance=±5% resistance=220 package=THT]
  R371 = Resistor [tolerance=±5% resistance=220 package=THT]
  R372 = Resistor [tolerance=±5% resistance=220 package=THT]
  R373 = Resistor [tolerance=±5% resistance=220 package=THT]
  R374 = Resistor [tolerance=±5% resistance=220 package=THT]
  R375 = Resistor [tolerance=±5% resistance=220 package=THT]
  J406 = female pin header, 39 pins [form="♀ (female)"]  # not connected
  J407 = female pin header, 39 pins [form="♀ (female)"]  # not connected
  IC22 = SELECTOR_MULTIPLEXER [package=dil16]  # not connected
  J408 = female pin header, 8 pins [form="♀ (female)"]  # not connected
  J409 = female pin header, 8 pins [form="♀ (female)"]  # not connected
  IC23 = SELECTOR_MULTIPLEXER [package=dil16]  # not connected
  J410 = female pin header, 8 pins [form="♀ (female)"]  # not connected
  J411 = female pin header, 8 pins [form="♀ (female)"]  # not connected
  IC24 = SELECTOR_MULTIPLEXER [package=dil16]
  IC26 = SELECTOR_MULTIPLEXER [package=dil16]
  IC27 = SELECTOR_MULTIPLEXER [package=dil16]
  IC28 = SELECTOR_MULTIPLEXER [package=dil16]
  IC29 = SELECTOR_MULTIPLEXER [package=dil16]
  IC30 = SELECTOR_MULTIPLEXER [package=dil16]
  Part1 = Arduino Mega 2560 (Rev3)
  IC25 = SELECTOR_MULTIPLEXER [package=dil16]

nets:
  N1: J404.pin2, R341.Pin_1, R344.Pin_0
  N2: J404.pin4, R341.Pin_0, R345.Pin_1
  N3: J404.pin6, R345.Pin_0, R352.Pin_1
  N4: J404.pin8, R336.Pin_1, R352.Pin_0
  N5: J404.pin10, R336.Pin_0, R343.Pin_1
  N6: J404.pin12, R343.Pin_0, R351.Pin_1
  N7: J404.pin14, R338.Pin_1, R351.Pin_0
  N8: J404.pin16, R338.Pin_0, R350.Pin_1
  N9: J404.pin18, R350.Pin_0, R354.Pin_1
  N10: J404.pin20, R354.Pin_0, R355.Pin_1
  N11: J404.pin22, R339.Pin_1, R355.Pin_0
  N12: J404.pin24, R339.Pin_0, R347.Pin_1
  N13: J404.pin26, R337.Pin_1, R347.Pin_0
  N14: J404.pin28, R337.Pin_0, R342.Pin_1
  N15: J404.pin30, R342.Pin_0, R348.Pin_1
  N16: J404.pin32, R346.Pin_1, R348.Pin_0
  N17: J404.pin34, R346.Pin_0, R353.Pin_1
  N18: J404.pin36, R349.Pin_1, R353.Pin_0
  N19: J404.pin38, R340.Pin_1, R349.Pin_0
  N20: J405.pin2, R365.Pin_1, R371.Pin_0
  N21: J405.pin4, R365.Pin_0, R374.Pin_1
  N22: J405.pin6, R359.Pin_1, R374.Pin_0
  N23: J405.pin8, R359.Pin_0, R361.Pin_1
  N24: J405.pin10, R361.Pin_0, R368.Pin_1
  N25: J405.pin12, R358.Pin_1, R368.Pin_0
  N26: J405.pin14, R356.Pin_1, R358.Pin_0
  N27: J405.pin16, R356.Pin_0, R360.Pin_1
  N28: J405.pin18, R360.Pin_0, R363.Pin_1
  N29: J405.pin20, R357.Pin_1, R363.Pin_0
  N30: J405.pin22, R357.Pin_0, R369.Pin_1
  N31: J405.pin24, R362.Pin_1, R369.Pin_0
  N32: J405.pin26, R362.Pin_0, R367.Pin_1
  N33: J405.pin28, R367.Pin_0, R372.Pin_1
  N34: J405.pin30, R372.Pin_0, R375.Pin_1
  N35: J405.pin32, R366.Pin_1, R375.Pin_0
  N36: J405.pin34, R366.Pin_0, R373.Pin_1
  N37: J405.pin36, R370.Pin_1, R373.Pin_0
  N38: J405.pin38, R364.Pin_1, R370.Pin_0
  N39: IC24.A_!A!_B, IC24.A_1A, IC24.A_G, IC24.P_VCC
  N40: IC24.A_1B, IC24.A_4A, IC30.A_2A, IC30.A_4Y
  N41: IC24.A_1Y, IC24.A_4B
  N42: IC24.A_2A, IC24.A_4Y
  N43: IC24.A_2B, IC24.A_2Y, IC24.A_3B, IC24.A_3A, IC26.A_2B, IC26.A_2Y, IC26.A_3B, IC26.A_3A, IC28.A_2B, IC28.A_2Y, IC28.A_3B, IC28.A_3A, Part1.5V
  N44: IC24.P_GND, IC24.A_3Y, IC26.P_GND, IC26.A_3Y, IC28.P_GND, IC28.A_3Y, Part1.D22
  N45: IC26.A_!A!_B, IC26.P_VCC
  N46: IC26.A_1A, IC26.A_G
  N47: IC26.A_1B, IC26.A_4A, IC30.A_2B, IC30.A_3A, Part1.D23
  N48: IC26.A_1Y, IC26.A_4B
  N49: IC26.A_2A, IC26.A_4Y
  N50: IC27.A_!A!_B, IC27.P_VCC
  N51: IC27.A_1A, IC27.A_G
  N52: IC27.A_1B, IC27.A_4A
  N53: IC27.A_1Y, IC27.A_4B
  N54: IC27.A_2A, IC27.A_4Y
  N55: IC27.A_2B, IC27.A_3A
  N56: IC27.A_2Y, IC27.A_3B
  N57: IC27.P_GND, IC27.A_3Y
  N58: IC28.A_!A!_B, IC28.P_VCC
  N59: IC28.A_1A, IC28.A_G
  N60: IC28.A_1B, IC28.A_4A, IC30.A_2Y, IC30.A_3B, Part1.D24
  N61: IC28.A_1Y, IC28.A_4B
  N62: IC28.A_2A, IC28.A_4Y
  N63: IC29.A_!A!_B, IC29.P_VCC
  N64: IC29.A_1A, IC29.A_G
  N65: IC29.A_1B, IC29.A_4A
  N66: IC29.A_1Y, IC29.A_4B
  N67: IC29.A_2A, IC29.A_4Y
  N68: IC29.A_2B, IC29.A_3A
  N69: IC29.A_2Y, IC29.A_3B
  N70: IC29.P_GND, IC29.A_3Y
  N71: IC30.A_!A!_B, IC30.P_VCC
  N72: IC30.A_1A, IC30.A_G
  N73: IC30.A_1B, IC30.A_4A
  N74: IC30.A_1Y, IC30.A_4B
  N75: IC30.P_GND, IC30.A_3Y, Part1.D25
  N76: IC25.A_!A!_B, IC25.P_VCC
  N77: IC25.A_1A, IC25.A_G
  N78: IC25.A_1B, IC25.A_4A
  N79: IC25.A_1Y, IC25.A_4B
  N80: IC25.A_2A, IC25.A_4Y
  N81: IC25.A_2B, IC25.A_3A
  N82: IC25.A_2Y, IC25.A_3B
  N83: IC25.P_GND, IC25.A_3Y

notes:
  lev3_selA
  lev3_selB
  lev3_selC
  lev2_selA
  lev2_selB
  lev2_selC
  lev1_selA
  lev1_selB
  lev1_selC
