# Fritzing sketch stripboard (saved by Fritzing 0.9.3b)
stripboards: 5
perfboards: 5

parts:
  IC1 = SELECTOR_MULTIPLEXER [package=dil16]
  J1 = female pin header, 8 pins [form="♀ (female)"]
  J2 = female pin header, 8 pins [form="♀ (female)"]
  IC2 = SELECTOR_MULTIPLEXER [package=dil16]
  J3 = female pin header, 8 pins [form="♀ (female)"]
  J4 = female pin header, 8 pins [form="♀ (female)"]
  IC3 = SELECTOR_MULTIPLEXER [package=dil16]
  J5 = female pin header, 8 pins [form="♀ (female)"]
  J6 = female pin header, 8 pins [form="♀ (female)"]
  R1 = Resistor [tolerance=±5% resistance=220 package=THT]
  R2 = Resistor [tolerance=±5% resistance=220 package=THT]
  R3 = Resistor [tolerance=±5% resistance=220 package=THT]
  R4 = Resistor [tolerance=±5% resistance=220 package=THT]
  R5 = Resistor [tolerance=±5% resistance=220 package=THT]
  R6 = Resistor [tolerance=±5% resistance=220 package=THT]
  R7 = Resistor [tolerance=±5% resistance=220 package=THT]
  R8 = Resistor [tolerance=±5% resistance=220 package=THT]
  R9 = Resistor [tolerance=±5% resistance=220 package=THT]
  R10 = Resistor [tolerance=±5% resistance=220 package=THT]
  R11 = Resistor [tolerance=±5% resistance=220 package=THT]
  R12 = Resistor [tolerance=±5% resistance=220 package=THT]
  R13 = Resistor [tolerance=±5% resistance=220 package=THT]
  R14 = Resistor [tolerance=±5% resistance=220 package=THT]
  R15 = Resistor [tolerance=±5% resistance=220 package=THT]
  R16 = Resistor [tolerance=±5% resistance=220 package=THT]
  R17 = Resistor [tolerance=±5% resistance=220 package=THT]
  R18 = Resistor [tolerance=±5% resistance=220 package=THT]
  R19 = Resistor [tolerance=±5% resistance=220 package=THT]
  R20 = Resistor [tolerance=±5% resistance=220 package=THT]
  R21 = Resistor [tolerance=±5% resistance=220 package=THT]
  J7 = female pin header, 2 pins [form="♀ (female)"]
  J8 = female pin header, 2 pins [form="♀ (female)"]
  J9 = female pin header, 2 pins [form="♀ (female)"]
  J10 = female pin header, 2 pins [form="♀ (female)"]
  J11 = female pin header, 2 pins [form="♀ (female)"]
  J12 = female pin header, 2 pins [form="♀ (female)"]
  J13 = female pin header, 2 pins [form="♀ (female)"]
  J14 = female pin header, 2 pins [form="♀ (female)"]
  J15 = female pin header, 2 pins [form="♀ (female)"]
  J16 = female pin header, 2 pins [form="♀ (female)"]
  J17 = female pin header, 2 pins [form="♀ (female)"]
  J18 = female pin header, 2 pins [form="♀ (female)"]
  J19 = female pin header, 2 pins [form="♀ (female)"]
  J20 = female pin header, 2 pins [form="♀ (female)"]
  J21 = female pin header, 2 pins [form="♀ (female)"]
  J22 = female pin header, 2 pins [form="♀ (female)"]
  J23 = female pin header, 2 pins [form="♀ (female)"]
  J24 = female pin header, 2 pins [form="♀ (female)"]
  J25 = female pin header, 2 pins [form="♀ (female)"]
  J26 = female pin header, 2 pins [form="♀ (female)"]
  R22 = Resistor [tolerance=±5% resistance=220 package=THT]
  R23 = Resistor [tolerance=±5% resistance=220 package=THT]
  R24 = Resistor [tolerance=±5% resistance=220 package=THT]
  R25 = Resistor [tolerance=±5% resistance=220 package=THT]
  R26 = Resistor [tolerance=±5% resistance=220 package=THT]
  R27 = Resistor [tolerance=±5% resistance=220 package=THT]
  R28 = Resistor [tolerance=±5% resistance=220 package=THT]
  R29 = Resistor [tolerance=±5% resistance=220 package=THT]
  R30 = Resistor [tolerance=±5% resistance=220 package=THT]
  R31 = Resistor [tolerance=±5% resistance=220 package=THT]
  R32 = Resistor [tolerance=±5% resistance=220 package=THT]
  R33 = Resistor [tolerance=±5% resistance=220 package=THT]
  R34 = Resistor [tolerance=±5% resistance=220 package=THT]
  R35 = Resistor [tolerance=±5% resistance=220 package=THT]
  R36 = Resistor [tolerance=±5% resistance=220 package=THT]
  R37 = Resistor [tolerance=±5% resistance=220 package=THT]
  R38 = Resistor [tolerance=±5% resistance=220 package=THT]
  R39 = Resistor [tolerance=±5% resistance=220 package=THT]
  R40 = Resistor [tolerance=±5% resistance=220 package=THT]
  R41 = Resistor [tolerance=±5% resistance=220 package=THT]
  R42 = Resistor [tolerance=±5% resistance=220 package=THT]
  IC4 = SELECTOR_MULTIPLEXER [package=dil16]
  J27 = female pin header, 8 pins [form="♀ (female)"]
  J28 = female pin header, 8 pins [form="♀ (female)"]
  IC5 = SELECTOR_MULTIPLEXER [package=dil16]
  J29 = female pin header, 8 pins [form="♀ (female)"]
  J30 = female pin header, 8 pins [form="♀ (female)"]
  IC6 = SELECTOR_MULTIPLEXER [package=dil16]
  J31 = female pin header, 8 pins [form="♀ (female)"]
  J32 = female pin header, 8 pins [form="♀ (female)"]
  J36 = female pin header, 2 pins [form="♀ (female)"]
  J37 = female pin header, 2 pins [form="♀ (female)"]
  J38 = female pin header, 2 pins [form="♀ (female)"]
  J39 = female pin header, 2 pins [form="♀ (female)"]
  J40 = female pin header, 2 pins [form="♀ (female)"]
  J41 = female pin header, 2 pins [form="♀ (female)"]
  J42 = female pin header, 2 pins [form="♀ (female)"]
  J43 = female pin header, 2 pins [form="♀ (female)"]
  J44 = female pin header, 2 pins [form="♀ (female)"]
  J45 = female pin header, 2 pins [form="♀ (female)"]
  J46 = female pin header, 2 pins [form="♀ (female)"]
  J47 = female pin header, 2 pins [form="♀ (female)"]
  J48 = female pin header, 2 pins [form="♀ (female)"]
  J49 = female pin header, 2 pins [form="♀ (female)"]
  J50 = female pin header, 2 pins [form="♀ (female)"]
  J51 = female pin header, 2 pins [form="♀ (female)"]
  J52 = female pin header, 2 pins [form="♀ (female)"]
  J53 = female pin header, 2 pins [form="♀ (female)"]
  J54 = female pin header, 2 pins [form="♀ (female)"]
  J55 = female pin header, 2 pins [form="♀ (female)"]
  J174 = female pin header, 1 pin [form="♀ (female)"]
  J180 = female pin header, 1 pin [form="♀ (female)"]
  J182 = female pin header, 1 pin [form="♀ (female)"]
  J183 = female pin header, 1 pin [form="♀ (female)"]
  J184 = female pin header, 1 pin [form="♀ (female)"]
  J185 = female pin header, 1 pin [form="♀ (female)"]
  J188 = female pin header, 1 pin [form="♀ (female)"]
  J189 = female pin header, 1 pin [form="♀ (female)"]
  J191 = female pin header, 1 pin [form="♀ (female)"]
  J194 = female pin header, 1 pin [form="♀ (female)"]
  J196 = female pin header, 1 pin [form="♀ (female)"]
  J197 = female pin header, 1 pin [form="♀ (female)"]
  J198 = female pin header, 1 pin [form="♀ (female)"]
  J199 = female pin header, 1 pin [form="♀ (female)"]
  J200 = female pin header, 1 pin [form="♀ (female)"]
  J201 = female pin header, 1 pin [form="♀ (female)"]
  R68 = Resistor [tolerance=±5% resistance=220 package=THT]
  R69 = Resistor [tolerance=±5% resistance=220 package=THT]
  R70 = Resistor [tolerance=±5% resistance=220 package=THT]
  R73 = Resistor [tolerance=±5% resistance=220 package=THT]
  R74 = Resistor [tolerance=±5% resistance=220 package=THT]
  R75 = Resistor [tolerance=±5% resistance=220 package=THT]
  R76 = Resistor [tolerance=±5% resistance=220 package=THT]
  R77 = Resistor [tolerance=±5% resistance=220 package=THT]
  R78 = Resistor [tolerance=±5% resistance=220 package=THT]
  R79 = Resistor [tolerance=±5% resistance=220 package=THT]
  R80 = Resistor [tolerance=±5% resistance=220 package=THT]
  R81 = Resistor [tolerance=±5% resistance=220 package=THT]
  R82 = Resistor [tolerance=±5% resistance=220 package=THT]
  R83 = Resistor [tolerance=±5% resistance=220 package=THT]
  R84 = Resistor [tolerance=±5% resistance=220 package=THT]
  R85 = Resistor [tolerance=±5% resistance=220 package=THT]
  R86 = Resistor [tolerance=±5% resistance=220 package=THT]
  J204 = female pin header, 1 pin [form="♀ (female)"]
  J205 = female pin header, 1 pin [form="♀ (female)"]
  R87 = Resistor [tolerance=±5% resistance=220 package=THT]
  R88 = Resistor [tolerance=±5% resistance=220 package=THT]
  J206 = female pin header, 1 pin [form="♀ (female)"]
  J207 = female pin header, 1 pin [form="♀ (female)"]
  R89 = Resistor [tolerance=±5% resistance=220 package=THT]
  R90 = Resistor [tolerance=±5% resistance=220 package=THT]
  R91 = Resistor [tolerance=±5% resistance=220 package=THT]
  R92 = Resistor [tolerance=±5% resistance=220 package=THT]
  R93 = Resistor [tolerance=±5% resistance=220 package=THT]
  R94 = Resistor [tolerance=±5% resistance=220 package=THT]
  R95 = Resistor [tolerance=±5% resistance=220 package=THT]
  R96 = Resistor [tolerance=±5% resistance=220 package=THT]
  R97 = Resistor [tolerance=±5% resistance=220 package=THT]
  R98 = Resistor [tolerance=±5% resistance=220 package=THT]
  R99 = Resistor [tolerance=±5% resistance=220 package=THT]
  R100 = Resistor [tolerance=±5% resistance=220 package=THT]
  R101 = Resistor [tolerance=±5% resistance=220 package=THT]
  R102 = Resistor [tolerance=±5% resistance=220 package=THT]
  R103 = Resistor [tolerance=±5% resistance=220 package=THT]
  R104 = Resistor [tolerance=±5% resistance=220 package=THT]
  R105 = Resistor [tolerance=±5% resistance=220 package=THT]
  R106 = Resistor [tolerance=±5% resistance=220 package=THT]
  R107 = Resistor [tolerance=±5% resistance=220 package=THT]
  R108 = Resistor [tolerance=±5% resistance=220 package=THT]
  R109 = Resistor [tolerance=±5% resistance=220 package=THT]
  R110 = Resistor [tolerance=±5% resistance=220 package=THT]
  J208 = female pin header, 1 pin [form="♀ (female)"]  # not connected
  J209 = female pin header, 1 pin [form="♀ (female)"]  # not connected
  J210 = female pin header, 1 pin [form="♀ (female)"]  # not connected
  J211 = female pin header, 1 pin [form="♀ (female)"]  # not connected
  J212 = female pin header, 1 pin [form="♀ (female)"]  # not connected
  J213 = female pin header, 1 pin [form="♀ (female)"]  # not connected
  J214 = female pin header, 1 pin [form="♀ (female)"]  # not connected
  J215 = female pin header, 1 pin [form="♀ (female)"]  # not connected
  J216 = female pin header, 1 pin [form="♀ (female)"]  # not connected
  J217 = female pin header, 1 pin [form="♀ (female)"]  # not connected
  J218 = female pin header, 1 pin [form="♀ (female)"]  # not connected
  J219 = female pin header, 1 pin [form="♀ (female)"]  # not connected
  J220 = female pin header, 1 pin [form="♀ (female)"]  # not connected
  J221 = female pin header, 1 pin [form="♀ (female)"]  # not connected
  J222 = female pin header, 1 pin [form="♀ (female)"]  # not connected
  J223 = female pin header, 1 pin [form="♀ (female)"]  # not connected
  J224 = female pin header, 1 pin [form="♀ (female)"]  # not connected
  J225 = female pin header, 1 pin [form="♀ (female)"]  # not connected
  J226 = female pin header, 1 pin [form="♀ (female)"]  # not connected
  J227 = female pin header, 1 pin [form="♀ (female)"]  # not connected
  IC7 = SELECTOR_MULTIPLEXER [package=dil16]  # not connected
  J228 = female pin header, 8 pins [form="♀ (female)"]
  J229 = female pin header, 8 pins [form="♀ (female)"]
  IC8 = SELECTOR_MULTIPLEXER [package=dil16]  # not connected
  J231 = female pin header, 8 pins [form="♀ (female)"]
  J232 = female pin header, 8 pins [form="♀ (female)"]
  IC9 = SELECTOR_MULTIPLEXER [package=dil16]  # not connected
  J233 = female pin header, 8 pins [form="♀ (female)"]  # not connected
  J234 = female pin header, 8 pins [form="♀ (female)"]  # not connected
  IC10 = SELECTOR_MULTIPLEXER [package=dil16]  # not connected
  J235 = female pin header, 8 pins [form="♀ (female)"]
  J236 = female pin header, 8 pins [form="♀ (female)"]
  IC11 = SELECTOR_MULTIPLEXER [package=dil16]  # not connected
  IC13 = SELECTOR_MULTIPLEXER [package=dil16]  # not connected
  IC14 = SELECTOR_MULTIPLEXER [package=dil16]  # not connected
  J237 = female pin header, 8 pins [form="♀ (female)"]  # not connected
  J238 = female pin header, 8 pins [form="♀ (female)"]  # not connected
  J240 = female pin header, 8 pins [form="♀ (female)"]  # not connected
  J241 = female pin header, 8 pins [form="♀ (female)"]  # not connected
  J242 = female pin header, 8 pins [form="♀ (female)"]  # not connected
  J243 = female pin header, 8 pins [form="♀ (female)"]
  IC15 = SELECTOR_MULTIPLEXER [package=dil16]  # not connected
  IC16 = SELECTOR_MULTIPLEXER [package=dil16]  # not connected
  IC17 = SELECTOR_MULTIPLEXER [package=dil16]  # not connected
  IC18 = SELECTOR_MULTIPLEXER [package=dil16]  # not connected
  IC19 = SELECTOR_MULTIPLEXER [package=dil16]  # not connected
  IC20 = SELECTOR_MULTIPLEXER [package=dil16]  # not connected
  IC21 = SELECTOR_MULTIPLEXER [package=dil16]  # not connected
  J244 = female pin header, 8 pins [form="♀ (female)"]  # not connected
  J245 = female pin header, 8 pins [form="♀ (female)"]  # not connected
  J246 = female pin header, 8 pins [form="♀ (female)"]  # not connected
  J247 = female pin header, 8 pins [form="♀ (female)"]  # not connected
  J248 = female pin header, 8 pins [form="♀ (female)"]  # not connected
  J249 = female pin header, 8 pins [form="♀ (female)"]  # not connected
  J250 = female pin header, 8 pins [form="♀ (female)"]  # not connected
  J251 = female pin header, 8 pins [form="♀ (female)"]  # not connected
  J252 = female pin header, 8 pins [form="♀ (female)"]  # not connected
  J253 = female pin header, 8 pins [form="♀ (female)"]  # not connected
  J254 = female pin header, 8 pins [form="♀ (female)"]  # not connected
  J255 = female pin header, 8 pins [form="♀ (female)"]  # not connected
  J256 = female pin header, 8 pins [form="♀ (female)"]  # not connected
  J257 = female pin header, 8 pins [form="♀ (female)"]  # not connected
  J258 = female pin header, 1 pin [form="♀ (female)"]
  J259 = female pin header, 1 pin [form="♀ (female)"]
  J260 = female pin header, 1 pin [form="♀ (female)"]
  J261 = female pin header, 1 pin [form="♀ (female)"]
  J262 = female pin header, 1 pin [form="♀ (female)"]
  J263 = female pin header, 1 pin [form="♀ (female)"]
  J264 = female pin header, 1 pin [form="♀ (female)"]
  J265 = female pin header, 1 pin [form="♀ (female)"]
  J266 = female pin header, 1 pin [form="♀ (female)"]
  J267 = female pin header, 1 pin [form="♀ (female)"]
  J268 = female pin header, 1 pin [form="♀ (female)"]
  J269 = female pin header, 1 pin [form="♀ (female)"]
  J270 = female pin header, 1 pin [form="♀ (female)"]
  J271 = female pin header, 1 pin [form="♀ (female)"]
  J272 = female pin header, 1 pin [form="♀ (female)"]
  J273 = female pin header, 1 pin [form="♀ (female)"]
  J274 = female pin header, 1 pin [form="♀ (female)"]
  J275 = female pin header, 1 pin [form="♀ (female)"]
  J276 = female pin header, 1 pin [form="♀ (female)"]
  J277 = female pin header, 1 pin [form="♀ (female)"]
  J278 = female pin header, 1 pin [form="♀ (female)"]  # not connected
  J279 = female pin header, 1 pin [form="♀ (female)"]  # not connected
  J280 = female pin header, 1 pin [form="♀ (female)"]  # not connected
  J281 = female pin header, 1 pin [form="♀ (female)"]  # not connected
  J282 = female pin header, 1 pin [form="♀ (female)"]  # not connected
  J283 = female pin header, 1 pin [form="♀ (female)"]  # not connected
  J284 = female pin header, 1 pin [form="♀ (female)"]
  J285 = female pin header, 1 pin [form="♀ (female)"]
  J286 = female pin header, 1 pin [form="♀ (female)"]
  J288 = female pin header, 1 pin [form="♀ (female)"]
  J289 = female pin header, 1 pin [form="♀ (female)"]  # not connected
  J290 = female pin header, 1 pin [form="♀ (female)"]  # not connected
  J291 = female pin header, 1 pin [form="♀ (female)"]  # not connected
  J292 = female pin header, 1 pin [form="♀ (female)"]  # not connected
  J293 = female pin header, 1 pin [form="♀ (female)"]
  J294 = female pin header, 1 pin [form="♀ (female)"]
  J295 = female pin header, 1 pin [form="♀ (female)"]
  J296 = female pin header, 1 pin [form="♀ (female)"]
  J297 = female pin header, 1 pin [form="♀ (female)"]  # not connected
  J287 = male pin header, 1 pin [form="♂ (male)"]
  J298 = female pin header, 1 pin [form="♀ (female)"]  # not connected
  J287_2 = female pin header, 1 pin [form="♀ (female)"]
  J299 = female pin header, 1 pin [form="♀ (female)"]  # not connected
  J300 = female pin header, 1 pin [form="♀ (female)"]  # not connected
  J301 = female pin header, 1 pin [form="♀ (female)"]
  J302 = female pin header, 1 pin [form="♀ (female)"]  # not connected
  J368 = male pin header, 39 pins [form="♂ (male)"]  # not connected
  J369 = male pin header, 39 pins [form="♂ (male)"]  # not connected
  R199 = Resistor [tolerance=±5% resistance=220 package=THT]  # not connected
  R200 = Resistor [tolerance=±5% resistance=220 package=THT]  # not connected
  R201 = Resistor [tolerance=±5% resistance=220 package=THT]  # not connected
  R202 = Resistor [tolerance=±5% resistance=220 package=THT]  # not connected
  R203 = Resistor [tolerance=±5% resistance=220 package=THT]  # not connected
  R204 = Resistor [tolerance=±5% resistance=220 package=THT]  # not connected
  R205 = Resistor [tolerance=±5% resistance=220 package=THT]  # not connected
  R206 = Resistor [tolerance=±5% resistance=220 package=THT]  # not connected
  R207 = Resistor [tolerance=±5% resistance=220 package=THT]  # not connected
  R208 = Resistor [tolerance=±5% resistance=220 package=THT]  # not connected
  R209 = Resistor [tolerance=±5% resistance=220 package=THT]  # not connected
  J370 = female pin header, 39 pins [form="♀ (female)"]  # not connected
  R210 = Resistor [tolerance=±5% resistance=220 package=THT]  # not connected
  J371 = female pin header, 39 pins [form="♀ (female)"]  # not connected
  R211 = Resistor [tolerance=±5% resistance=220 package=THT]  # not connected
  R212 = Resistor [tolerance=±5% resistance=220 package=THT]  # not connected
  R213 = Resistor [tolerance=±5% resistance=220 package=THT]  # not connected
  R214 = Resistor [tolerance=±5% resistance=220 package=THT]  # not connected
  R215 = Resistor [tolerance=±5% resistance=220 package=THT]  # not connected
  R216 = Resistor [tolerance=±5% resistance=220 package=THT]  # not connected
  R217 = Resistor [tolerance=±5% resistance=220 package=THT]  # not connected
  R218 = Resistor [tolerance=±5% resistance=220 package=THT]  # not connected
  R219 = Resistor [tolerance=±5% resistance=220 package=THT]  # not connected
  R220 = Resistor [tolerance=±5% resistance=220 package=THT]  # not connected
  R221 = Resistor [tolerance=±5% resistance=220 package=THT]  # not connected
  R222 = Resistor [tolerance=±5% resistance=220 package=THT]  # not connected
  R223 = Resistor [tolerance=±5% resistance=220 package=THT]  # not connected
  R224 = Resistor [tolerance=±5% resistance=220 package=THT]  # not connected
  R225 = Resistor [tolerance=±5% resistance=220 package=THT]  # not connected
  R226 = Resistor [tolerance=±5% resistance=220 package=THT]  # not connected
  R227 = Resistor [tolerance=±5% resistance=220 package=THT]  # not connected
  R228 = Resistor [tolerance=±5% resistance=220 package=THT]  # not connected
  R229 = Resistor [tolerance=±5% resistance=220 package=THT]  # not connected
  R230 = Resistor [tolerance=±5% resistance=220 package=THT]  # not connected
  R231 = Resistor [tolerance=±5% resistance=220 package=THT]  # not connected
  R232 = Resistor [tolerance=±5% resistance=220 package=THT]  # not connected
  R233 = Resistor [tolerance=±5% resistance=220 package=THT]  # not connected
  R234 = Resistor [tolerance=±5% resistance=220 package=THT]  # not connected
  R235 = Resistor [tolerance=±5% resistance=220 package=THT]  # not connected
  R236 = Resistor [tolerance=±5% resistance=220 package=THT]  # not connected
  R237 = Resistor [tolerance=±5% resistance=220 package=THT]  # not connected
  R238 = Resistor [tolerance=±5% resistance=220 package=THT]  # not connected
  R239 = Resistor [tolerance=±5% resistance=220 package=THT]  # not connected
  R240 = Resistor [tolerance=±5% resistance=220 package=THT]  # not connected
  IC36 = SELECTOR_MULTIPLEXER [package=dil16]  # not connected
  IC37 = SELECTOR_MULTIPLEXER [package=dil16]  # not connected
  IC38 = SELECTOR_MULTIPLEXER [package=dil16]  # not connected
  IC39 = SELECTOR_MULTIPLEXER [package=dil16]  # not connected
  IC40 = SELECTOR_MULTIPLEXER [package=dil16]  # not connected
  IC41 = SELECTOR_MULTIPLEXER [package=dil16]  # not connected
  IC42 = SELECTOR_MULTIPLEXER [package=dil16]  # not connected
  J372 = female pin header, 8 pins [form="♀ (female)"]  # not connected
  J373 = female pin header, 8 pins [form="♀ (female)"]  # not connected
  J374 = female pin header, 8 pins [form="♀ (female)"]  # not connected
  J375 = female pin header, 8 pins [form="♀ (female)"]  # not connected
  J376 = female pin header, 8 pins [form="♀ (female)"]  # not connected
  J377 = female pin header, 8 pins [form="♀ (female)"]  # not connected
  J378 = female pin header, 8 pins [form="♀ (female)"]  # not connected
  J379 = female pin header, 8 pins [form="♀ (female)"]  # not connected
  J380 = female pin header, 8 pins [form="♀ (female)"]  # not connected
  J381 = female pin header, 8 pins [form="♀ (female)"]  # not connected
  J382 = female pin header, 8 pins [form="♀ (female)"]  # not connected
  J383 = female pin header, 8 pins [form="♀ (female)"]  # not connected
  J384 = female pin header, 8 pins [form="♀ (female)"]  # not connected
  J385 = female pin header, 8 pins [form="♀ (female)"]  # not connected
  J386 = female pin header, 8 pins [form="♀ (female)"]  # not connected
  J387 = female pin header, 8 pins [form="♀ (female)"]  # not connected
  J388 = female pin header, 8 pins [form="♀ (female)"]  # not connected
  J389 = female pin header, 8 pins [form="♀ (female)"]  # not connected
  J390 = female pin header, 8 pins [form="♀ (female)"]  # not connected
  J391 = female pin header, 8 pins [form="♀ (female)"]  # not connected
  J392 = female pin header, 8 pins [form="♀ (female)"]  # not connected
  J393 = female pin header, 8 pins [form="♀ (female)"]  # not connected
  J394 = female pin header, 8 pins [form="♀ (female)"]  # not connected
  J395 = female pin header, 8 pins [form="♀ (female)"]  # not connected
  J396 = female pin header, 8 pins [form="♀ (female)"]  # not connected
  J397 = female pin header, 8 pins [form="♀ (female)"]  # not connected
  J398 = female pin header, 8 pins [form="♀ (female)"]  # not connected
  J399 = female pin header, 8 pins [form="♀ (female)"]  # not connected
  J400 = double row male pin header, 48 pins [form="♂ (male)"]
  R241 = Resistor [tolerance=±5% resistance=220 package=THT]
  R242 = Resistor [tolerance=±5% resistance=220 package=THT]
  R243 = Resistor [tolerance=±5% resistance=220 package=THT]
  R244 = Resistor [tolerance=±5% resistance=220 package=THT]
  R245 = Resistor [tolerance=±5% resistance=220 package=THT]
  R246 = Resistor [tolerance=±5% resistance=220 package=THT]
  R247 = Resistor [tolerance=±5% resistance=220 package=THT]
  R248 = Resistor [tolerance=±5% resistance=220 package=THT]
  R249 = Resistor [tolerance=±5% resistance=220 package=THT]
  R250 = Resistor [tolerance=±5% resistance=220 package=THT]
  R251 = Resistor [tolerance=±5% resistance=220 package=THT]
  R252 = Resistor [tolerance=±5% resistance=220 package=THT]
  R253 = Resistor [tolerance=±5% resistance=220 package=THT]
  R254 = Resistor [tolerance=±5% resistance=220 package=THT]
  R255 = Resistor [tolerance=±5% resistance=220 package=THT]
  R256 = Resistor [tolerance=±5% resistance=220 package=THT]
  R257 = Resistor [tolerance=±5% resistance=220 package=THT]
  R258 = Resistor [tolerance=±5% resistance=220 package=THT]
  R259 = Resistor [tolerance=±5% resistance=220 package=THT]
  R260 = Resistor [tolerance=±5% resistance=220 package=THT]
  R261 = Resistor [tolerance=±5% resistance=220 package=THT]
  R262 = Resistor [tolerance=±5% resistance=220 package=THT]
  R263 = Resistor [tolerance=±5% resistance=220 package=THT]
  R264 = Resistor [tolerance=±5% resistance=220 package=THT]
  R265 = Resistor [tolerance=±5% resistance=220 package=THT]
  R266 = Resistor [tolerance=±5% resistance=220 package=THT]
  R267 = Resistor [tolerance=±5% resistance=220 package=THT]
  R268 = Resistor [tolerance=±5% resistance=220 package=THT]
  R269 = Resistor [tolerance=±5% resistance=220 package=THT]
  R270 = Resistor [tolerance=±5% resistance=220 package=THT]
  R271 = Resistor [tolerance=±5% resistance=220 package=THT]
  R272 = Resistor [tolerance=±5% resistance=220 package=THT]
  R273 = Resistor [tolerance=±5% resistance=220 package=THT]
  R274 = Resistor [tolerance=±5% resistance=220 package=THT]
  R275 = Resistor [tolerance=±5% resistance=220 package=THT]
  R276 = Resistor [tolerance=±5% resistance=220 package=THT]
  R277 = Resistor [tolerance=±5% resistance=220 package=THT]
  R278 = Resistor [tolerance=±5% resistance=220 package=THT]
  R279 = Resistor [tolerance=±5% resistance=220 package=THT]
  R280 = Resistor [tolerance=±5% resistance=220 package=THT]
  R281 = Resistor [tolerance=±5% resistance=220 package=THT]
  R282 = Resistor [tolerance=±5% resistance=220 package=THT]
  J401 = double row male pin header, 46 pins [form="♂ (male)"]
  J402 = male pin header, 39 pins [form="♂ (male)"]
  J403 = male pin header, 39 pins [form="♂ (male)"]
  R283 = Resistor [tolerance=±5% resistance=220 package=THT]
  R297 = Resistor [tolerance=±5% resistance=220 package=THT]
  R298 = Resistor [tolerance=±5% resistance=220 package=THT]
  R299 = Resistor [tolerance=±5% resistance=220 package=THT]
  R300 = Resistor [tolerance=±5% resistance=220 package=THT]
  R301 = Resistor [tolerance=±5% resistance=220 package=THT]
  R302 = Resistor [tolerance=±5% resistance=220 package=THT]
  R303 = Resistor [tolerance=±5% resistance=220 package=THT]
  R304 = Resistor [tolerance=±5% resistance=220 package=THT]
  R305 = Resistor [tolerance=±5% resistance=220 package=THT]
  R306 = Resistor [tolerance=±5% resistance=220 package=THT]
  R307 = Resistor [tolerance=±5% resistance=220 package=THT]
  R308 = Resistor [tolerance=±5% resistance=220 package=THT]
  R309 = Resistor [tolerance=±5% resistance=220 package=THT]
  R310 = Resistor [tolerance=±5% resistance=220 package=THT]
  R311 = Resistor [tolerance=±5% resistance=220 package=THT]
  R312 = Resistor [tolerance=±5% resistance=220 package=THT]
  R313 = Resistor [tolerance=±5% resistance=220 package=THT]
  R314 = Resistor [tolerance=±5% resistance=220 package=THT]
  R315 = Resistor [tolerance=±5% resistance=220 package=THT]
  R316 = Resistor [tolerance=±5% resistance=220 package=THT]
  R317 = Resistor [tolerance=±5% resistance=220 package=THT]
  R318 = Resistor [tolerance=±5% resistance=220 package=THT]
  R319 = Resistor [tolerance=±5% resistance=220 package=THT]
  R320 = Resistor [tolerance=±5% resistance=220 package=THT]
  R321 = Resistor [tolerance=±5% resistance=220 package=THT]
  R322 = Resistor [tolerance=±5% resistance=220 package=THT]
  R323 = Resistor [tolerance=±5% resistance=220 package=THT]
  R324 = Resistor [tolerance=±5% resistance=220 package=THT]
  R325 = Resistor [tolerance=±5% resistance=220 package=THT]
  R326 = Resistor [tolerance=±5% resistance=220 package=THT]
  R327 = Resistor [tolerance=±5% resistance=220 package=THT]
  R328 = Resistor [tolerance=±5% resistance=220 package=THT]
  R329 = Resistor [tolerance=±5% resistance=220 package=THT]
  R330 = Resistor [tolerance=±5% resistance=220 package=THT]
  R331 = Resistor [tolerance=±5% resistance=220 package=THT]
  R332 = Resistor [tolerance=±5% resistance=220 package=THT]
  R333 = Resistor [tolerance=±5% resistance=220 package=THT]
  R334 = Resistor [tolerance=±5% resistance=220 package=THT]
  R335 = Resistor [tolerance=±5% resistance=220 package=THT]
  R336 = Resistor [tolerance=±5% resistance=220 package=THT]
  R337 = Resistor [tolerance=±5% resistance=220 package=THT]
  R338 = Resistor [tolerance=±5% resistance=220 package=THT]
  R339 = Resistor [tolerance=±5% resistance=220 package=THT]
  R340 = Resistor [tolerance=±5% resistance=220 package=THT]
  R341 = Resistor [tolerance=±5% resistance=220 package=THT]
  R342 = Resistor [tolerance=±5% resistance=220 package=THT]
  R343 = Resistor [tolerance=±5% resistance=220 package=THT]
  R344 = Resistor [tolerance=±5% resistance=220 package=THT]
  R345 = Resistor [tolerance=±5% resistance=220 package=THT]
  R346 = Resistor [tolerance=±5% resistance=220 package=THT]
  R347 = Resistor [tolerance=±5% resistance=220 package=THT]
  R348 = Resistor [tolerance=±5% resistance=220 package=THT]
  R349 = Resistor [tolerance=±5% resistance=220 package=THT]
  R350 = Resistor [tolerance=±5% resistance=220 package=THT]
  R351 = Resistor [tolerance=±5% resistance=220 package=THT]
  R353 = Resistor [tolerance=±5% resistance=220 package=THT]
  R354 = Resistor [tolerance=±5% resistance=220 package=THT]
  R355 = Resistor [tolerance=±5% resistance=220 package=THT]
  R356 = Resistor [tolerance=±5% resistance=220 package=THT]
  R357 = Resistor [tolerance=±5% resistance=220 package=THT]
  R358 = Resistor [tolerance=±5% resistance=220 package=THT]
  R359 = Resistor [tolerance=±5% resistance=220 package=THT]
  R360 = Resistor [tolerance=±5% resistance=220 package=THT]
  R361 = Resistor [tolerance=±5% resistance=220 package=THT]
  R362 = Resistor [tolerance=±5% resistance=220 package=THT]
  R363 = Resistor [tolerance=±5% resistance=220 package=THT]
  R364 = Resistor [tolerance=±5% resistance=220 package=THT]
  R365 = Resistor [tolerance=±5% resistance=220 package=THT]
  R366 = Resistor [tolerance=±5% resistance=220 package=THT]
  R367 = Resistor [tolerance=±5% resistance=220 package=THT]
  R368 = Resistor [tolerance=±5% resistance=220 package=THT]
  R369 = Resistor [tolerance=±5% resistance=220 package=THT]
  R371 = Resistor [tolerance=±5% resistance=220 package=THT]
  R373 = Resistor [tolerance=±5% resistance=220 package=THT]
  R376 = Resistor [tolerance=±5% resistance=220 package=THT]
  R377 = Resistor [tolerance=±5% resistance=220 package=THT]
  R378 = Resistor [tolerance=±5% resistance=220 package=THT]
  R380 = Resistor [tolerance=±5% resistance=220 package=THT]
  R381 = Resistor [tolerance=±5% resistance=220 package=THT]

nets:
  N1: IC1.A_!A!_B, J2.pin1
  N2: IC1.A_1A, J2.pin2
  N3: IC1.A_1B, J2.pin3
  N4: IC1.A_1Y, J2.pin4
  N5: IC1.A_2A, J2.pin5
  N6: IC1.A_2B, J2.pin6
  N7: IC1.A_2Y, J2.pin7
  N8: IC1.P_GND, J2.pin8
  N9: IC1.A_3Y, J1.pin8
  N10: IC1.A_3B, J1.pin7
  N11: IC1.A_3A, J1.pin6
  N12: IC1.A_4Y, J1.pin5
  N13: IC1.A_4B, J1.pin4
  N14: IC1.A_4A, J1.pin3
  N15: IC1.A_G, J1.pin2
  N16: IC1.P_VCC, J1.pin1
  N17: IC2.A_!A!_B, J3.pin1
  N18: IC2.A_1A, J3.pin2
  N19: IC2.A_1B, J3.pin3
  N20: IC2.A_1Y, J3.pin4
  N21: IC2.A_2A, J3.pin5
  N22: IC2.A_2B, J3.pin6
  N23: IC2.A_2Y, J3.pin7
  N24: IC2.P_GND, J3.pin8
  N25: IC2.A_3Y, J4.pin8
  N26: IC2.A_3B, J4.pin7
  N27: IC2.A_3A, J4.pin6
  N28: IC2.A_4Y, J4.pin5
  N29: IC2.A_4B, J4.pin4
  N30: IC2.A_4A, J4.pin3
  N31: IC2.A_G, J4.pin2
  N32: IC2.P_VCC, J4.pin1
  N33: IC3.A_!A!_B, J5.pin1
  N34: IC3.A_1A, J5.pin2
  N35: IC3.A_1B, J5.pin3
  N36: IC3.A_1Y, J5.pin4
  N37: IC3.A_2A, J5.pin5
  N38: IC3.A_2B, J5.pin6
  N39: IC3.A_2Y, J5.pin7
  N40: IC3.P_GND, J5.pin8
  N41: IC3.A_3Y, J6.pin8
  N42: IC3.A_3B, J6.pin7
  N43: IC3.A_3A, J6.pin6
  N44: IC3.A_4Y, J6.pin5
  N45: IC3.A_4B, J6.pin4
  N46: IC3.A_4A, J6.pin3
  N47: IC3.A_G, J6.pin2
  N48: IC3.P_VCC, J6.pin1
  N49: R1.Pin_1, R2.Pin_0, J7.pin1, J7.pin2
  N50: R2.Pin_1, R3.Pin_0, J8.pin1, J8.pin2
  N51: R3.Pin_1, R4.Pin_0, J9.pin1, J9.pin2
  N52: R4.Pin_1, R5.Pin_0, J10.pin1, J10.pin2
  N53: R5.Pin_1, J11.pin1
  N54: R6.Pin_0, J11.pin2
  N55: R6.Pin_1, R7.Pin_0, J14.pin1, J14.pin2
  N56: R7.Pin_1, R8.Pin_0, J15.pin1, J15.pin2
  N57: R8.Pin_1, R9.Pin_0, J13.pin1, J13.pin2
  N58: R9.Pin_1, R10.Pin_0, J12.pin1, J12.pin2
  N59: R10.Pin_1, R20.Pin_0, J16.pin1, J16.pin2
  N60: R11.Pin_0, R20.Pin_1, J19.pin1, J19.pin2
  N61: R11.Pin_1, R19.Pin_0, J20.pin1, J20.pin2
  N62: R12.Pin_0, R18.Pin_1, J25.pin1, J25.pin2
  N63: R12.Pin_1, R15.Pin_0, J23.pin1, J23.pin2
  N64: R13.Pin_0, R17.Pin_1, J17.pin1, J17.pin2
  N65: R13.Pin_1, R16.Pin_0, J21.pin1, J21.pin2
  N66: R14.Pin_0, R15.Pin_1, J22.pin1, J22.pin2
  N67: R14.Pin_1, R21.Pin_0, J26.pin1, J26.pin2
  N68: R16.Pin_1, R18.Pin_0, J24.pin1, J24.pin2
  N69: R17.Pin_0, R19.Pin_1, J18.pin1, J18.pin2
  N70: R22.Pin_0, J37.pin2
  N71: R23.Pin_0, J44.pin2
  N72: R23.Pin_1, J55.pin1
  N73: R24.Pin_0, J42.pin1, J42.pin2
  N74: R24.Pin_1, J48.pin1, J48.pin2
  N75: R25.Pin_0, J49.pin2
  N76: R25.Pin_1, J45.pin1
  N77: R26.Pin_0, J41.pin2
  N78: R26.Pin_1, J46.pin1
  N79: R27.Pin_0, J51.pin2
  N80: R27.Pin_1, J50.pin1
  N81: R28.Pin_0, J45.pin2
  N82: R28.Pin_1, J39.pin1
  N83: R29.Pin_1, J38.pin1
  N84: R30.Pin_0, J47.pin2
  N85: R30.Pin_1, J37.pin1
  N86: R31.Pin_0, J40.pin2
  N87: R31.Pin_1, J53.pin1
  N88: R32.Pin_0, J43.pin2
  N89: R32.Pin_1, J52.pin1
  N90: R33.Pin_0, J36.pin2
  N91: R33.Pin_1, J49.pin1
  N92: R34.Pin_0, J55.pin2
  N93: R34.Pin_1, J43.pin1
  N94: R35.Pin_0, J52.pin2
  N95: R36.Pin_0, J53.pin2
  N96: R36.Pin_1, J44.pin1
  N97: R37.Pin_0, J54.pin2
  N98: R37.Pin_1, J41.pin1
  N99: R38.Pin_1, J36.pin1
  N100: R39.Pin_0, J50.pin2
  N101: R39.Pin_1, J40.pin1
  N102: R40.Pin_0, J39.pin2
  N103: R40.Pin_1, J54.pin1
  N104: R41.Pin_0, J46.pin2
  N105: R41.Pin_1, J47.pin1
  N106: R42.Pin_0, J38.pin2
  N107: R42.Pin_1, J51.pin1
  N108: IC4.A_!A!_B, IC4.P_VCC, J27.pin1, J28.pin1
  N109: IC4.A_1A, IC4.A_G, J27.pin2, J28.pin2
  N110: IC4.A_1B, IC4.A_4A, J27.pin3, J28.pin3
  N111: IC4.A_1Y, IC4.A_4B, J27.pin4, J28.pin4
  N112: IC4.A_2A, IC4.A_4Y, J27.pin5, J28.pin5
  N113: IC4.A_2B, IC4.A_3A, J27.pin6, J28.pin6
  N114: IC4.A_2Y, IC4.A_3B, J27.pin7, J28.pin7
  N115: IC4.P_GND, IC4.A_3Y, J27.pin8, J28.pin8
  N116: IC5.A_!A!_B, IC5.P_VCC, J29.pin1, J30.pin1
  N117: IC5.A_1A, IC5.A_G, J29.pin2, J30.pin2
  N118: IC5.A_1B, IC5.A_4A, J29.pin3, J30.pin3
  N119: IC5.A_1Y, IC5.A_4B, J29.pin4, J30.pin4
  N120: IC5.A_2A, IC5.A_4Y, J29.pin5, J30.pin5
  N121: IC5.A_2B, IC5.A_3A, J29.pin6, J30.pin6
  N122: IC5.A_2Y, IC5.A_3B, J29.pin7, J30.pin7
  N123: IC5.P_GND, IC5.A_3Y, J29.pin8, J30.pin8
  N124: IC6.A_!A!_B, IC6.P_VCC, J31.pin1, J32.pin1
  N125: IC6.A_1A, IC6.A_G, J31.pin2, J32.pin2
  N126: IC6.A_1B, IC6.A_4A, J31.pin3, J32.pin3
  N127: IC6.A_1Y, IC6.A_4B, J31.pin4, J32.pin4
  N128: IC6.A_2A, IC6.A_4Y, J31.pin5, J32.pin5
  N129: IC6.A_2B, IC6.A_3A, J31.pin6, J32.pin6
  N130: IC6.A_2Y, IC6.A_3B, J31.pin7, J32.pin7
  N131: IC6.P_GND, IC6.A_3Y, J31.pin8, J32.pin8
  N132: J174.pin1, J180.pin1, J182.pin1, J183.pin1, J184.pin1, J185.pin1, J188.pin1, J189.pin1, J191.pin1, J194.pin1, J196.pin1, J197.pin1, J198.pin1, J199.pin1, J200.pin1, J201.pin1, R68.Pin_0, R68.Pin_1, R69.Pin_0, R69.Pin_1, R70.Pin_0, R70.Pin_1, R73.Pin_0, R73.Pin_1, R74.Pin_0, R74.Pin_1, R75.Pin_0, R75.Pin_1, R76.Pin_0, R76.Pin_1, R77.Pin_0, R77.Pin_1, R78.Pin_0, R78.Pin_1, R79.Pin_0, R79.Pin_1, R80.Pin_0, R80.Pin_1, R81.Pin_0, R81.Pin_1, R82.Pin_0, R82.Pin_1, R83.Pin_0, R83.Pin_1, R84.Pin_0, R84.Pin_1, R85.Pin_0, R85.Pin_1, R86.Pin_0, R86.Pin_1, J204.pin1, J205.pin1, R87.Pin_0, R87.Pin_1, R88.Pin_0, R88.Pin_1, J206.pin1, J207.pin1, R89.Pin_0, R89.Pin_1
  N133: R90.Pin_0, R90.Pin_1
  N134: R91.Pin_0, R91.Pin_1
  N135: R92.Pin_0, R92.Pin_1
  N136: R93.Pin_0, R93.Pin_1
  N137: R94.Pin_0, R94.Pin_1
  N138: R95.Pin_0, R95.Pin_1
  N139: R96.Pin_0, R96.Pin_1
  N140: R97.Pin_0, R97.Pin_1
  N141: R98.Pin_0, R98.Pin_1
  N142: R99.Pin_0, R99.Pin_1
  N143: R100.Pin_0, R100.Pin_1
  N144: R101.Pin_0, R101.Pin_1
  N145: R102.Pin_0, R102.Pin_1
  N146: R103.Pin_0, R103.Pin_1
  N147: R104.Pin_0, R104.Pin_1
  N148: R105.Pin_0, R105.Pin_1
  N149: R106.Pin_0, R106.Pin_1
  N150: R107.Pin_0, R107.Pin_1
  N151: R108.Pin_0, R108.Pin_1
  N152: R109.Pin_0, R109.Pin_1
  N153: R110.Pin_0, R110.Pin_1
  N154: J228.pin4, J262.pin1
  N155: J228.pin5, J263.pin1
  N156: J228.pin7, J264.pin1
  N157: J228.pin8, J265.pin1
  N158: J229.pin4, J261.pin1
  N159: J229.pin5, J258.pin1
  N160: J229.pin6, J259.pin1
  N161: J229.pin7, J260.pin1
  N162: J229.pin8, J301.pin1
  N163: J231.pin4, J295.pin1
  N164: J231.pin5, J285.pin1
  N165: J231.pin7, J296.pin1
  N166: J231.pin8, J293.pin1
  N167: J232.pin4, J294.pin1
  N168: J232.pin5, J288.pin1
  N169: J232.pin6, J284.pin1
  N170: J232.pin7, J286.pin1
  N171: J235.pin4, J270.pin1
  N172: J235.pin5, J267.pin1
  N173: J235.pin7, J271.pin1
  N174: J235.pin8, J266.pin1
  N175: J236.pin4, J269.pin1
  N176: J236.pin5, J272.pin1
  N177: J236.pin6, J268.pin1
  N178: J236.pin7, J273.pin1
  N179: J243.pin4, J276.pin1
  N180: J243.pin5, J275.pin1
  N181: J243.pin6, J277.pin1
  N182: J243.pin7, J274.pin1
  N183: J287.pin1, J287_2.pin1
  N184: J400.pin1, J400.pin3, R256.Pin_0, R276.Pin_0
  N185: J400.pin6, J400.pin8, R248.Pin_0, R270.Pin_0
  N186: J400.pin11, J400.pin13, R244.Pin_0, R261.Pin_0
  N187: J400.pin16, J400.pin18, R254.Pin_0, R257.Pin_0
  N188: J400.pin21, J400.pin23, R249.Pin_0, R282.Pin_0
  N189: J400.pin26, J400.pin28, R242.Pin_0, R260.Pin_0
  N190: J400.pin31, J400.pin33, R268.Pin_0, R273.Pin_0
  N191: J400.pin36, J400.pin38, R265.Pin_0, R280.Pin_0
  N192: J400.pin41, J400.pin43, R245.Pin_0, R252.Pin_0
  N193: J400.pin46, J400.pin48, R264.Pin_0, R272.Pin_0
  N194: R241.Pin_0, R259.Pin_0
  N195: R241.Pin_1, R281.Pin_1
  N196: R242.Pin_1, R282.Pin_1, J401.pin21, J401.pin24
  N197: R243.Pin_0, R262.Pin_0
  N198: R243.Pin_1, R258.Pin_1
  N199: R244.Pin_1, R257.Pin_1, J401.pin11, J401.pin14
  N200: R245.Pin_1, R264.Pin_1, J401.pin41, J401.pin44
  N201: R246.Pin_0, R251.Pin_0
  N202: R246.Pin_1, R263.Pin_1
  N203: R247.Pin_0, R269.Pin_0
  N204: R247.Pin_1, R262.Pin_1
  N205: R248.Pin_1, R261.Pin_1, J401.pin6, J401.pin9
  N206: R249.Pin_1, R254.Pin_1, J401.pin16, J401.pin19
  N207: R250.Pin_0, R281.Pin_0
  N208: R250.Pin_1, R253.Pin_1
  N209: R251.Pin_1, R266.Pin_1
  N210: R252.Pin_1, R265.Pin_1, J401.pin36, J401.pin39
  N211: R253.Pin_0, R258.Pin_0
  N212: R255.Pin_0, R275.Pin_0
  N213: R255.Pin_1, R256.Pin_1
  N214: R259.Pin_1, R274.Pin_1
  N215: R260.Pin_1, R273.Pin_1, J401.pin26, J401.pin29
  N216: R263.Pin_0, R271.Pin_0
  N217: R266.Pin_0, R279.Pin_0
  N218: R267.Pin_0, R274.Pin_0
  N219: R267.Pin_1, R279.Pin_1
  N220: R268.Pin_1, R280.Pin_1, J401.pin31, J401.pin34
  N221: R269.Pin_1, R275.Pin_1
  N222: R270.Pin_1, R276.Pin_1, J401.pin1, J401.pin4
  N223: R271.Pin_1, R278.Pin_1
  N224: R272.Pin_1, R277.Pin_1, J401.pin46
  N225: R277.Pin_0, R278.Pin_0
  N226: J402.pin2, R283.Pin_0, R298.Pin_1
  N227: J402.pin4, R298.Pin_0, R300.Pin_1
  N228: J402.pin6, R300.Pin_0, R301.Pin_1
  N229: J402.pin8, R301.Pin_0, R307.Pin_1
  N230: J402.pin10, R304.Pin_1, R307.Pin_0
  N231: J402.pin12, R304.Pin_0, R305.Pin_1
  N232: J402.pin14, R305.Pin_0, R306.Pin_1
  N233: J402.pin16, R306.Pin_0, R315.Pin_1
  N234: J402.pin18, R312.Pin_1, R315.Pin_0
  N235: J402.pin20, R312.Pin_0, R313.Pin_1
  N236: J402.pin22, R313.Pin_0, R314.Pin_1
  N237: J402.pin24, R314.Pin_0, R323.Pin_1
  N238: J402.pin26, R320.Pin_1, R323.Pin_0
  N239: J402.pin28, R320.Pin_0, R321.Pin_1
  N240: J402.pin30, R321.Pin_0, R322.Pin_1
  N241: J402.pin32, R322.Pin_0, R331.Pin_1
  N242: J402.pin34, R328.Pin_1, R331.Pin_0
  N243: J402.pin36, R328.Pin_0, R329.Pin_1
  N244: J402.pin38, R329.Pin_0, R330.Pin_1
  N245: J403.pin2, R297.Pin_0, R299.Pin_1
  N246: J403.pin4, R299.Pin_0, R303.Pin_1
  N247: J403.pin6, R302.Pin_1, R303.Pin_0
  N248: J403.pin8, R302.Pin_0, R309.Pin_1
  N249: J403.pin10, R309.Pin_0, R310.Pin_1
  N250: J403.pin12, R308.Pin_1, R310.Pin_0
  N251: J403.pin14, R308.Pin_0, R311.Pin_1
  N252: J403.pin16, R311.Pin_0, R317.Pin_1
  N253: J403.pin18, R317.Pin_0, R318.Pin_1
  N254: J403.pin20, R316.Pin_1, R318.Pin_0
  N255: J403.pin22, R316.Pin_0, R319.Pin_1
  N256: J403.pin24, R319.Pin_0, R325.Pin_1
  N257: J403.pin26, R325.Pin_0, R326.Pin_1
  N258: J403.pin28, R324.Pin_1, R326.Pin_0
  N259: J403.pin30, R324.Pin_0, R327.Pin_1
  N260: J403.pin32, R327.Pin_0, R333.Pin_1
  N261: J403.pin34, R333.Pin_0, R334.Pin_1
  N262: J403.pin36, R332.Pin_1, R334.Pin_0
  N263: J403.pin38, R332.Pin_0, R335.Pin_1
  N264: R336.Pin_0, R339.Pin_1
  N265: R337.Pin_0, R338.Pin_1
  N266: R338.Pin_0, R342.Pin_1
  N267: R339.Pin_0, R343.Pin_1
  N268: R340.Pin_0, R347.Pin_1
  N269: R340.Pin_1, R343.Pin_0
  N270: R341.Pin_0, R346.Pin_1
  N271: R341.Pin_1, R342.Pin_0
  N272: R344.Pin_0, R355.Pin_1
  N273: R344.Pin_1, R347.Pin_0
  N274: R345.Pin_0, R358.Pin_1
  N275: R345.Pin_1, R346.Pin_0
  N276: R348.Pin_0, R353.Pin_1
  N277: R348.Pin_1, R354.Pin_0
  N278: R349.Pin_0, R356.Pin_1
  N279: R349.Pin_1, R358.Pin_0
  N280: R350.Pin_0, R357.Pin_1
  N281: R350.Pin_1, R356.Pin_0
  N282: R351.Pin_0, R354.Pin_1
  N283: R351.Pin_1, R355.Pin_0
  N284: R353.Pin_0, R366.Pin_1
  N285: R357.Pin_0, R369.Pin_1
  N286: R359.Pin_0, R364.Pin_1
  N287: R359.Pin_1, R365.Pin_0
  N288: R360.Pin_0, R367.Pin_1
  N289: R360.Pin_1, R369.Pin_0
  N290: R361.Pin_0, R368.Pin_1
  N291: R361.Pin_1, R367.Pin_0
  N292: R362.Pin_0, R365.Pin_1
  N293: R362.Pin_1, R366.Pin_0
  N294: R363.Pin_0, R380.Pin_1
  N295: R363.Pin_1, R368.Pin_0
  N296: R364.Pin_0, R381.Pin_1
  N297: R371.Pin_0, R378.Pin_1
  N298: R371.Pin_1, R380.Pin_0
  N299: R373.Pin_0, R376.Pin_1
  N300: R373.Pin_1, R377.Pin_0
  N301: R377.Pin_1, R381.Pin_0

notes:
  Put extra gap between resistors for contacts
